// Logisim project II_CSE_012_Ass_10_Q1.circ as structural Verilog: 1 circuit, main circuit main
module main (
  input  A1,
  input  A0,
  input  B1,
  input  B0
);

  wire and_1_out, and_2_out, and_3_out, and_4_out, and_5_out, and_6_out, bin_to_dec_1_a_2, bin_to_dec_1_b_2,
       bin_to_dec_1_c_2, bin_to_dec_1_d_2, bin_to_dec_1_e, bin_to_dec_1_f, bin_to_dec_1_g, xor_1_out,
       xor_2_out;

  and and_1 (and_1_out, A0, B0);
  and and_2 (and_2_out, A0, B1);
  and and_3 (and_3_out, B0, A1);
  and and_4 (and_4_out, B1, A1);
  xor xor_1 (xor_1_out, and_2_out, and_3_out);
  and and_5 (and_5_out, and_2_out, and_3_out);
  xor xor_2 (xor_2_out, and_4_out, and_5_out);
  and and_6 (and_6_out, and_4_out, and_5_out);
  bin_to_dec bin_to_dec_1 (
    .D(and_6_out), .C(xor_2_out), .B(xor_1_out), .A(and_1_out), .a_2(bin_to_dec_1_a_2),
    .b_2(bin_to_dec_1_b_2), .c_2(bin_to_dec_1_c_2), .d_2(bin_to_dec_1_d_2), .e(bin_to_dec_1_e),
    .f(bin_to_dec_1_f), .g(bin_to_dec_1_g));
  _7_Segment_Display u_7_segment_display_1 (
    .g(bin_to_dec_1_g), .f(bin_to_dec_1_f), .a(bin_to_dec_1_a_2), .b(bin_to_dec_1_b_2), .e(bin_to_dec_1_e),
    .d(bin_to_dec_1_d_2), .c(bin_to_dec_1_c_2), .dp(1'b0));

  // Notes on the sheet:
  //   MULTIPLICAND
  //   MULTIPLIER
  //   HALF ADDER
  //   HALF ADDER
  //   SUM
  //   CARRY
  //   SUM
  //   CARRY
endmodule
