// Logisim project II_CSE_012_Ass_11_Q1.circ as structural Verilog: 1 circuit, main circuit main
module main (
  input  [3:0] X,
  input  [3:0] Y,
  output [7:0] out_3
);

  wire adder_1_cout, adder_2_cout, adder_2_out, adder_3_cout, adder_3_out, adder_4_cout, adder_4_out,
       adder_5_cout, adder_6_cout, adder_6_out, adder_7_cout, adder_7_out, adder_8_cout, adder_8_out,
       adder_9_cout, adder_10_cout, adder_11_cout, and_2_out, and_3_out, and_4_out, and_5_out, and_6_out,
       and_7_out, and_8_out, and_9_out, and_10_out, and_11_out, and_12_out, and_13_out, and_14_out,
       and_15_out, and_16_out;

  and and_1 (out_3[0], X[0], Y[0]);
  and and_2 (and_2_out, X[1], Y[0]);
  and and_3 (and_3_out, X[0], Y[1]);
  and and_4 (and_4_out, X[2], Y[0]);
  and and_5 (and_5_out, X[1], Y[1]);
  and and_6 (and_6_out, X[3], Y[0]);
  and and_7 (and_7_out, X[2], Y[1]);
  and and_8 (and_8_out, X[3], Y[1]);
  and and_9 (and_9_out, X[3], Y[2]);
  Adder #(.width(1)) adder_1 (.a(and_2_out), .b(and_3_out), .out(out_3[1]), .cin(1'b0), .cout(adder_1_cout));
  Adder #(.width(1)) adder_2 (.a(and_4_out), .b(and_5_out), .out(adder_2_out), .cin(adder_1_cout), .cout(adder_2_cout));
  Adder #(.width(1)) adder_3 (.a(and_6_out), .b(and_7_out), .out(adder_3_out), .cin(adder_2_cout), .cout(adder_3_cout));
  Adder #(.width(1)) adder_4 (.a(adder_3_cout), .b(and_8_out), .out(adder_4_out), .cout(adder_4_cout));  // open: cin
  and and_10 (and_10_out, X[3], Y[3]);
  and and_11 (and_11_out, X[0], Y[2]);
  and and_12 (and_12_out, X[1], Y[2]);
  and and_13 (and_13_out, X[2], Y[2]);
  Adder #(.width(1)) adder_5 (.a(adder_2_out), .b(and_11_out), .out(out_3[2]), .cin(1'b0), .cout(adder_5_cout));
  Adder #(.width(1)) adder_6 (
    .a(adder_3_out), .b(and_12_out), .out(adder_6_out), .cin(adder_5_cout), .cout(adder_6_cout));
  Adder #(.width(1)) adder_7 (
    .a(adder_4_out), .b(and_13_out), .out(adder_7_out), .cin(adder_6_cout), .cout(adder_7_cout));
  Adder #(.width(1)) adder_8 (
    .a(adder_4_cout), .b(and_9_out), .out(adder_8_out), .cin(adder_7_cout), .cout(adder_8_cout));
  and and_14 (and_14_out, X[0], Y[3]);
  and and_15 (and_15_out, X[1], Y[3]);
  Adder #(.width(1)) adder_9 (.a(adder_6_out), .b(and_14_out), .out(out_3[3]), .cin(1'b0), .cout(adder_9_cout));
  Adder #(.width(1)) adder_10 (
    .a(adder_7_out), .b(and_15_out), .out(out_3[4]), .cin(adder_9_cout), .cout(adder_10_cout));
  Adder #(.width(1)) adder_11 (
    .a(adder_8_out), .b(and_16_out), .out(out_3[5]), .cin(adder_10_cout), .cout(adder_11_cout));
  and and_16 (and_16_out, X[2], Y[3]);
  Adder #(.width(1)) adder_12 (.a(adder_8_cout), .b(and_10_out), .out(out_3[6]), .cin(adder_11_cout), .cout(out_3[7]));

  // Notes on the sheet:
  //   INPUT 2 [X & Y] 4 BIT NUMBERS IN BINARY
  //   Assignment 11 [U19CS012]
  //   4 - BIT MULTIPLIER
  //   OUTPUT
endmodule
