// Logisim project IICSE_012_Ass012_01.circ as structural Verilog: 1 circuit, main circuit main
module main (
  input  [2:0] Read_Select_1,
  input  [2:0] Read_Select_2,
  input  [2:0] Write_Select,
  input  [15:0] Write_Data,
  output [15:0] out_5,
  output [15:0] out_6
);

  wire CLOCK_out;
  wire [15:0] demultiplexer_1_out0, demultiplexer_1_out1, demultiplexer_1_out2, demultiplexer_1_out3,
       demultiplexer_1_out4, demultiplexer_1_out5, demultiplexer_1_out6, demultiplexer_1_out7, R0_q, R1_q,
       R2_q, R3_q, R4_q, R5_q, R6_q, R7_q;

  Clock CLOCK (.out(CLOCK_out));
  Demultiplexer #(.select(3), .width(16)) demultiplexer_1 (
    .out0(demultiplexer_1_out0), .out1(demultiplexer_1_out1), .out2(demultiplexer_1_out2),
    .out3(demultiplexer_1_out3), .out4(demultiplexer_1_out4), .out5(demultiplexer_1_out5),
    .out6(demultiplexer_1_out6), .out7(demultiplexer_1_out7), .in(Write_Data), .sel(Write_Select));  // open: en
  Register #(.width(16)) R0 (.D(demultiplexer_1_out0), .Q(R0_q), .clk(CLOCK_out));  // open: en, clr
  Register #(.width(16)) R1 (.D(demultiplexer_1_out1), .Q(R1_q), .clk(CLOCK_out));  // open: en, clr
  Register #(.width(16)) R2 (.D(demultiplexer_1_out2), .Q(R2_q), .clk(CLOCK_out));  // open: en, clr
  Register #(.width(16)) R3 (.D(demultiplexer_1_out3), .Q(R3_q), .clk(CLOCK_out));  // open: en, clr
  Register #(.width(16)) R4 (.D(demultiplexer_1_out4), .Q(R4_q), .clk(CLOCK_out));  // open: en, clr
  Register #(.width(16)) R5 (.D(demultiplexer_1_out5), .Q(R5_q), .clk(CLOCK_out));  // open: en, clr
  Register #(.width(16)) R6 (.D(demultiplexer_1_out6), .Q(R6_q), .clk(CLOCK_out));  // open: en, clr
  Register #(.width(16)) R7 (.D(demultiplexer_1_out7), .Q(R7_q), .clk(CLOCK_out));  // open: en, clr
  Multiplexer #(.select(3), .width(16)) multiplexer_1 (
    .in0(R0_q), .in1(R1_q), .in2(R2_q), .in3(R3_q), .in4(R4_q), .in5(R5_q), .in6(R6_q), .in7(R7_q),
    .out(out_5), .sel(Read_Select_1));  // open: en
  Multiplexer #(.select(3), .width(16)) multiplexer_2 (
    .in0(R0_q), .in1(R1_q), .in2(R2_q), .in3(R3_q), .in4(R4_q), .in5(R5_q), .in6(R6_q), .in7(R7_q),
    .out(out_6), .sel(Read_Select_2));  // open: en

  // Notes on the sheet:
  //   ASSIGNMENT-12 Q-1
  //   8x16 - Bit  Register File
  //   U19CS012
endmodule
