// Logisim project IICSE_012_Ass012_02.circ as structural Verilog: 1 circuit, main circuit main
module main (
  input  [2:0] GATE_SELECTOR,
  input  [7:0] INPUT_1,
  input  [7:0] INPUT_2,
  output [7:0] OUTPUT,
  output CARRY,
  output OVERFLOW,
  output NEGATIVE,
  output ZERO_OUTPUT
);

  wire comparator_1_lt, comparator_2_lt;
  wire [7:0] adder_1_out, AND_out, bit_extender_1_out, bit_extender_2_out, NOR_out, OR_out, subtractor_1_out,
       XOR_out;

  Adder adder_1 (.a(INPUT_1), .b(INPUT_2), .out(adder_1_out), .cout(CARRY));  // open: cin
  Subtractor subtractor_1 (.a(INPUT_1), .b(INPUT_2), .out(subtractor_1_out), .bout(OVERFLOW));  // open: bin
  Comparator comparator_1 (.a(INPUT_1), .b(INPUT_2), .lt(comparator_1_lt));  // open: gt, eq
  Comparator #(.mode("unsigned")) comparator_2 (.a(INPUT_1), .b(INPUT_2), .lt(comparator_2_lt));  // open: gt, eq
  assign AND_out = INPUT_1 & INPUT_2;  // AND_Gate AND, 8 bits wide
  assign OR_out = INPUT_1 | INPUT_2;  // OR_Gate OR, 8 bits wide
  assign XOR_out = INPUT_1 ^ INPUT_2;  // XOR_Gate XOR, 8 bits wide
  assign NOR_out = ~(INPUT_1 | INPUT_2);  // NOR_Gate NOR, 8 bits wide
  assign bit_extender_1_out = {{7{1'b0}}, comparator_1_lt};  // Bit_Extender bit_extender_1
  assign bit_extender_2_out = {{7{1'b0}}, comparator_2_lt};  // Bit_Extender bit_extender_2
  Multiplexer #(.select(3), .width(8)) multiplexer_1 (
    .in0(adder_1_out), .in1(subtractor_1_out), .in2(bit_extender_1_out), .in3(bit_extender_2_out),
    .in4(AND_out), .in5(OR_out), .in6(XOR_out), .in7(NOR_out), .out({NEGATIVE, OUTPUT[6:0]}),
    .sel(GATE_SELECTOR));  // open: en
  Comparator #(.mode("unsigned")) comparator_3 (
    .a({NEGATIVE, OUTPUT[6:0]}), .b({8{1'b0}}), .eq(ZERO_OUTPUT));  // open: gt, lt

  assign OUTPUT[7] = NEGATIVE;

  // Notes on the sheet:
  //   ASSIGNMENT 12  Q-2
  //   8-BIT ALU [8 OPERATIONS] 
  //   U19CS012
endmodule
