// Logisim project Full_Adder.circ as structural Verilog
module Full_Adder (
  input  A,
  input  B,
  input  CIN,
  output SUM,
  output Cout
);

  wire and_1_out, and_2_out, and_3_out, and_4_out, and_5_out, and_6_out, and_7_out, and_8_out, and_9_out,
       and_10_out, and_11_out, not_1_out, not_2_out, not_3_out, not_4_out, not_5_out, not_6_out, not_7_out;

  and and_1 (and_1_out, A, B);
  not not_1 (not_1_out, and_1_out);
  and and_2 (and_2_out, CIN, A);
  and and_3 (and_3_out, CIN, B);
  and and_4 (and_4_out, B, A);
  and and_5 (and_5_out, A, not_1_out);
  not not_2 (not_2_out, and_5_out);
  not not_3 (not_3_out, and_6_out);
  and and_6 (and_6_out, not_1_out, B);
  and and_7 (and_7_out, not_2_out, not_3_out);
  or or_1 (Cout, and_2_out, and_3_out, and_4_out);
  not not_4 (not_4_out, and_7_out);
  and and_8 (and_8_out, not_4_out, CIN);
  not not_5 (not_5_out, and_8_out);
  and and_9 (and_9_out, not_4_out, not_5_out);
  not not_6 (not_6_out, and_9_out);
  and and_10 (and_10_out, not_5_out, CIN);
  not not_7 (not_7_out, and_10_out);
  and and_11 (and_11_out, not_6_out, not_7_out);
  not not_8 (SUM, and_11_out);

  // Notes on the sheet:
  //   A
  //   B
  //   Input Carry
  //   Output Cout
  //   SUM
endmodule
