// Logisim project Half_Adder.circ as structural Verilog
module Half_Adder (
  input  in_1,
  input  in_2,
  output SUM,
  output CARRY
);

  wire and_2_out, and_3_out, and_4_out, and_5_out, not_1_out, not_2_out, not_3_out;

  and and_1 (CARRY, in_1, in_2);
  and and_2 (and_2_out, in_1, in_2);
  not not_1 (not_1_out, and_2_out);
  and and_3 (and_3_out, in_1, not_1_out);
  and and_4 (and_4_out, not_1_out, in_2);
  not not_2 (not_2_out, and_3_out);
  not not_3 (not_3_out, and_4_out);
  and and_5 (and_5_out, not_2_out, not_3_out);
  not not_4 (SUM, and_5_out);

  // Notes on the sheet:
  //   CARRY
  //   SUM
endmodule
