// Logisim project IICSE_012_Ass03_04.circ as structural Verilog
module Full_Adder (
  input  A,
  input  B,
  input  BIN,
  output Diff,
  output Bout
);

  wire and_1_out, and_2_out, and_3_out, and_4_out, and_5_out, and_6_out, and_7_out, and_8_out, and_9_out,
       and_10_out, and_11_out, not_1_out, not_2_out, not_3_out, not_4_out, not_5_out, not_6_out, not_7_out,
       not_8_out;

  not not_1 (not_1_out, A);
  and and_1 (and_1_out, A, B);
  not not_2 (not_2_out, and_1_out);
  and and_2 (and_2_out, not_1_out, B);
  and and_3 (and_3_out, B, BIN);
  and and_4 (and_4_out, not_1_out, BIN);
  and and_5 (and_5_out, A, not_2_out);
  not not_3 (not_3_out, and_5_out);
  not not_4 (not_4_out, and_6_out);
  and and_6 (and_6_out, not_2_out, B);
  and and_7 (and_7_out, not_3_out, not_4_out);
  or or_1 (Bout, and_2_out, and_3_out, and_4_out);
  not not_5 (not_5_out, and_7_out);
  and and_8 (and_8_out, not_5_out, BIN);
  not not_6 (not_6_out, and_8_out);
  and and_9 (and_9_out, not_5_out, not_6_out);
  not not_7 (not_7_out, and_9_out);
  and and_10 (and_10_out, not_6_out, BIN);
  not not_8 (not_8_out, and_10_out);
  and and_11 (and_11_out, not_7_out, not_8_out);
  not not_9 (Diff, and_11_out);

  // Notes on the sheet:
  //   A
  //   B
  //   Input Borrow
  //   Borrow Out
  //   DIFFERENCE
endmodule
