// Logisim project Circuit1.circ as structural Verilog
module _4_bit_half_adder (
  input  CARRY_IN,
  input  A0,
  input  A1,
  input  A2,
  input  A3,
  input  B0,
  input  B1,
  input  B2,
  input  B3,
  output SUM_0,
  output SUM_1,
  output SUM_2,
  output SUM_3,
  output CARRY_OUT
);

  Adder #(.width(1)) adder_1 (.a(A0), .b(B0), .out(SUM_0));  // open: cin, cout
  Adder #(.width(1)) adder_2 (.a(A1), .b(B1), .out(SUM_1));  // open: cin, cout
  Adder #(.width(1)) adder_3 (.a(A2), .b(B2), .out(SUM_2));  // open: cin, cout
  Adder #(.width(1)) adder_4 (.a(A3), .b(B3), .out(SUM_3));  // open: cin, cout

  // Notes on the sheet:
  //   4 BIT HALF ADDER
endmodule
