// Logisim project Circuit3.circ as structural Verilog
module _4_bit_half_subtractor (
  input  BORROW__IN,
  input  A0,
  input  A1,
  input  A2,
  input  A3,
  input  B0,
  input  B1,
  input  B2,
  input  B3,
  output SUB_0,
  output SUB_1,
  output SUB_2,
  output SUB_3,
  output BORROW_OUT
);

  wire subtractor_4_bout;

  Subtractor #(.width(1)) subtractor_1 (.a(A0), .b(B0), .out(SUB_0));  // open: bin, bout
  Subtractor #(.width(1)) subtractor_2 (.a(A1), .b(B1), .out(SUB_1));  // open: bin, bout
  Subtractor #(.width(1)) subtractor_3 (.a(A2), .b(B2), .out(SUB_2));  // open: bin, bout
  Subtractor #(.width(1)) subtractor_4 (.a(A3), .b(B3), .out(SUB_3), .bout(subtractor_4_bout));  // open: bin

  // Notes on the sheet:
  //   4 BIT HALF SUBTRACTOR
endmodule
