// Logisim project Circuit8.circ as structural Verilog
module _8_BIT_Full_Subtractor (
  input  BORROW_IN,
  input  A0,
  input  A1,
  input  A2,
  input  A3,
  input  A4,
  input  A5,
  input  A6,
  input  A7,
  input  B0,
  input  B1,
  input  B2,
  input  B3,
  input  B4,
  input  B5,
  input  B6,
  input  B7,
  output DIFF_0,
  output DIFF_1,
  output DIFF_2,
  output DIFF_3,
  output DIFF_4,
  output DIFF_5,
  output DIFF_6,
  output DIFF_7,
  output BORROW_OUT
);

  wire subtractor_1_bout, subtractor_2_bout, subtractor_3_bout, subtractor_4_bout, subtractor_5_bout,
       subtractor_6_bout, subtractor_7_bout, subtractor_8_bout, undriven;

  Subtractor #(.width(1)) subtractor_1 (.a(A0), .b(B0), .out(DIFF_0), .bin(undriven), .bout(subtractor_1_bout));
  Subtractor #(.width(1)) subtractor_2 (
    .a(A1), .b(B1), .out(DIFF_1), .bin(subtractor_1_bout), .bout(subtractor_2_bout));
  Subtractor #(.width(1)) subtractor_3 (
    .a(A2), .b(B2), .out(DIFF_2), .bin(subtractor_2_bout), .bout(subtractor_3_bout));
  Subtractor #(.width(1)) subtractor_4 (
    .a(A3), .b(B3), .out(DIFF_3), .bin(subtractor_3_bout), .bout(subtractor_4_bout));
  Subtractor #(.width(1)) subtractor_5 (
    .a(A4), .b(B4), .out(DIFF_4), .bin(subtractor_4_bout), .bout(subtractor_5_bout));
  Subtractor #(.width(1)) subtractor_6 (
    .a(A5), .b(B5), .out(DIFF_5), .bin(subtractor_5_bout), .bout(subtractor_6_bout));
  Subtractor #(.width(1)) subtractor_7 (
    .a(A6), .b(B6), .out(DIFF_6), .bin(subtractor_6_bout), .bout(subtractor_7_bout));
  Subtractor #(.width(1)) subtractor_8 (
    .a(A7), .b(B7), .out(DIFF_7), .bin(subtractor_7_bout), .bout(subtractor_8_bout));

  // Notes on the sheet:
  //   8 BIT FULL SUBTRACTOR
endmodule
