// Logisim project IICSE_012_Ass3_1_04.circ as structural Verilog
module _4_bit_full_Subtractor (
  input  BORROW__IN,
  input  A0,
  input  A1,
  input  A2,
  input  A3,
  input  B0,
  input  B1,
  input  B2,
  input  B3,
  output SUB_0,
  output SUB_1,
  output SUB_2,
  output SUB_3,
  output BORROW_OUT
);

  wire subtractor_1_bout, subtractor_2_bout, subtractor_3_bout, subtractor_4_bout, undriven;

  Subtractor #(.width(1)) subtractor_1 (.a(A0), .b(B0), .out(SUB_0), .bin(undriven), .bout(subtractor_1_bout));
  Subtractor #(.width(1)) subtractor_2 (.a(A1), .b(B1), .out(SUB_1), .bin(subtractor_1_bout), .bout(subtractor_2_bout));
  Subtractor #(.width(1)) subtractor_3 (.a(A2), .b(B2), .out(SUB_2), .bin(subtractor_2_bout), .bout(subtractor_3_bout));
  Subtractor #(.width(1)) subtractor_4 (.a(A3), .b(B3), .out(SUB_3), .bin(subtractor_3_bout), .bout(subtractor_4_bout));

  // Notes on the sheet:
  //   4 BIT FULL SUBTRACTOR
endmodule
