// Logisim project IICSE_012_Ass3_1_05.circ as structural Verilog
module _8_bit_Half_Adder (
  input  CARRY_IN,
  input  A0,
  input  A1,
  input  A2,
  input  A3,
  input  A4,
  input  A5,
  input  A6,
  input  A7,
  input  B0,
  input  B1,
  input  B2,
  input  B3,
  input  B4,
  input  B5,
  input  B6,
  input  B7,
  output SUM_0,
  output SUM_1,
  output SUM_2,
  output SUM_3,
  output SUM_4,
  output SUM_5,
  output SUM_6,
  output SUM_7,
  output CARRY_OUT
);

  wire adder_8_cout;

  Adder #(.width(1)) adder_1 (.a(A0), .b(B0), .out(SUM_0));  // open: cin, cout
  Adder #(.width(1)) adder_2 (.a(A1), .b(B1), .out(SUM_1));  // open: cin, cout
  Adder #(.width(1)) adder_3 (.a(A2), .b(B2), .out(SUM_2));  // open: cin, cout
  Adder #(.width(1)) adder_4 (.a(A3), .b(B3), .out(SUM_3));  // open: cin, cout
  Adder #(.width(1)) adder_5 (.a(A4), .b(B4), .out(SUM_4));  // open: cin, cout
  Adder #(.width(1)) adder_6 (.a(A5), .b(B5), .out(SUM_5));  // open: cin, cout
  Adder #(.width(1)) adder_7 (.a(A6), .b(B6), .out(SUM_6));  // open: cin, cout
  Adder #(.width(1)) adder_8 (.a(A7), .b(B7), .out(SUM_7), .cout(adder_8_cout));  // open: cin

  // Notes on the sheet:
  //   8 BIT HALF ADDER
endmodule
