// Logisim project IICSE_012_Ass3_1_06.circ as structural Verilog
module _8_bit_Half_Subtracotrr (
  input  BORROW_IN,
  input  A0,
  input  A1,
  input  A2,
  input  A3,
  input  A4,
  input  A5,
  input  A6,
  input  A7,
  input  B0,
  input  B1,
  input  B2,
  input  B3,
  input  B4,
  input  B5,
  input  B6,
  input  B7,
  output SUM_0,
  output SUM_1,
  output SUM_2,
  output SUM_3,
  output SUM_4,
  output SUM_5,
  output SUM_6,
  output SUM_7,
  output BORROW_OUT
);

  Subtractor #(.width(1)) subtractor_1 (.a(A0), .b(B0), .out(SUM_0));  // open: bin, bout
  Subtractor #(.width(1)) subtractor_2 (.a(A1), .b(B1), .out(SUM_1));  // open: bin, bout
  Subtractor #(.width(1)) subtractor_3 (.a(A2), .b(B2), .out(SUM_2));  // open: bin, bout
  Subtractor #(.width(1)) subtractor_4 (.a(A3), .b(B3), .out(SUM_3));  // open: bin, bout
  Subtractor #(.width(1)) subtractor_5 (.a(A4), .b(B4), .out(SUM_4));  // open: bin, bout
  Subtractor #(.width(1)) subtractor_6 (.a(A5), .b(B5), .out(SUM_5));  // open: bin, bout
  Subtractor #(.width(1)) subtractor_7 (.a(A6), .b(B6), .out(SUM_6));  // open: bin, bout
  Subtractor #(.width(1)) subtractor_8 (.a(A7), .b(B7), .out(SUM_7));  // open: bin, bout

  // Notes on the sheet:
  //   8 BIT HALF SUBTRACTOR
endmodule
