// Logisim project IICSE_012_Ass_1_f.circ as structural Verilog: 1 circuit, main circuit main
module main (
  input  [7:0] X,
  input  [7:0] Y,
  output [7:0] out_3
);

  Negator negator_1 (.in(X), .out(out_3));

  // Notes on the sheet:
  //   INPUT = X
  //   NEGATOR
  //   OUTPUT = -X (2's Complement)
endmodule
