// Logisim project IICSE_012_Ass_1_a.circ as structural Verilog: 1 circuit, main circuit main
module main (
  input  [7:0] X,
  input  [7:0] Y,
  output [7:0] out_3
);

  Adder adder_1 (.a(X), .b(X), .out(out_3));  // open: cin, cout

  // Notes on the sheet:
  //   INPUT = X
  //   ADDER
  //   OUTPUT = 2X
endmodule
