// Logisim project IICSE_012_Ass_1_b.circ as structural Verilog: 1 circuit, main circuit main
module main (
  input  [7:0] X,
  input  [7:0] Y,
  output [7:0] out_3
);

  wire [7:0] adder_1_out;

  Adder adder_1 (.a(X), .b(X), .out(adder_1_out));  // open: cin, cout
  Adder adder_2 (.a(adder_1_out), .b(Y), .out(out_3));  // open: cin, cout

  // Notes on the sheet:
  //   INPUT = X
  //   INPUT = Y
  //   ADDER
  //   ADDER
  //   OUTPUT = 2X + Y
endmodule
