// Logisim project IICSE_012_Ass_1_c.circ as structural Verilog: 1 circuit, main circuit main
module main (
  input  [7:0] X,
  input  [7:0] Y,
  output [7:0] out_3
);

  wire [7:0] adder_1_out;

  Adder adder_1 (.a(X), .b(Y), .out(adder_1_out));  // open: cin, cout
  Divider divider_1 (.a(adder_1_out), .b(8'h2), .out(out_3));  // open: upper, rem

  // Notes on the sheet:
  //   INPUT = X
  //   INPUT = Y
  //   ADDER
  //   DIVIDER
  //   OUTPUT = (X + Y)/2
endmodule
