// Logisim project IICSE_012_Ass_1_g.circ as structural Verilog: 1 circuit, main circuit main
module main (
  input  [7:0] X,
  input  [7:0] Y,
  output [7:0] out_3
);

  wire [7:0] multiplier_1_out, multiplier_2_out;

  Multiplier multiplier_1 (.a(X), .b(X), .out(multiplier_1_out));  // open: cin, cout
  Multiplier multiplier_2 (.a(multiplier_1_out), .b(multiplier_1_out), .out(multiplier_2_out));  // open: cin, cout
  Multiplier multiplier_3 (.a(multiplier_2_out), .b(multiplier_1_out), .out(out_3));  // open: cin, cout

  // Notes on the sheet:
  //   INPUT = X
  //   MULTIPLIER
  //   MULTIPLIER
  //   MULTIPLIER
  //   OUTPUT = (X)^6
endmodule
