// Logisim project IICSE_012_Ass_8_1.circ as structural Verilog: 1 circuit, main circuit main
module main (
  input  [7:0] A,
  input  [7:0] X,
  input  [7:0] Y,
  output [7:0] AX_Y
);

  wire [7:0] main_1_out_3;

  IICSE_012_Ass_1_e_main main_1 (.X(A), .Y(X), .out_3(main_1_out_3));
  Adder adder_1 (.a(main_1_out_3), .b(Y), .out(AX_Y));  // open: cin, cout

  // Notes on the sheet:
  //   Imported from Ass 7
  //   A.X
  //   ADDER
  //   OUTPUT: AX+Y
endmodule
