// Logisim project IICSE_012_Ass_8_2.circ as structural Verilog: 1 circuit, main circuit main
module main (
  input  [7:0] A,
  input  [7:0] B,
  input  [7:0] C,
  input  [7:0] D,
  output [7:0] AVG
);

  wire [7:0] main_1_out_3, main_2_out_3;

  IICSE_012_Ass_1_c_main main_1 (.X(A), .Y(B), .out_3(main_1_out_3));
  IICSE_012_Ass_1_c_main main_2 (.X(C), .Y(D), .out_3(main_2_out_3));
  IICSE_012_Ass_1_c_main main_3 (.X(main_1_out_3), .Y(main_2_out_3), .out_3(AVG));

  // Notes on the sheet:
  //   (A+B)/2
  //   (C+D)/2
  //   ((A+B)/2 + (C+D)/2)/2
  //   OUTPUT : (A+B+C+D)/4 [Even]
endmodule
