// Logisim project IICSE_012_Ass_8_3.circ as structural Verilog: 1 circuit, main circuit main
module main (
  input  [7:0] X,
  input  [7:0] Y,
  output [7:0] X_Y__2
);

  wire [7:0] adder_1_out, main_1_out_3, main_2_out_3, main_3_out_3, main_4_out_3;

  IICSE_012_Ass_1_d_main main_1 (.X(X), .Y(X), .out_3(main_1_out_3));
  IICSE_012_Ass_1_d_main main_2 (.X(Y), .Y(Y), .out_3(main_2_out_3));
  IICSE_012_Ass_1_e_main main_3 (.X(X), .Y(Y), .out_3(main_3_out_3));
  IICSE_012_Ass_1_a_main main_4 (.X(main_3_out_3), .Y(8'h2), .out_3(main_4_out_3));
  Adder adder_1 (.a(main_1_out_3), .b(main_4_out_3), .out(adder_1_out));  // open: cin, cout
  Adder adder_2 (.a(adder_1_out), .b(main_2_out_3), .out(X_Y__2));  // open: cin, cout

  // Notes on the sheet:
  //   X^2
  //   Y^2
  //   (X)x(Y)
  //   2x(XY)
  //   X^2 + 2XY
  //   X^2 + 2XY + Y^2
endmodule
