// Logisim project IICSE_012_Ass_8_4.circ as structural Verilog: 1 circuit, main circuit main
module main (
  input  [7:0] X,
  output [7:0] _4__X_prime____4X
);

  wire [7:0] main_1_out_3, main_2_out_3, main_3_out_3;

  IICSE_012_Ass_1_f_main main_1 (.X(X), .out_3(main_1_out_3));  // open: Y
  IICSE_012_Ass_1_a_main main_2 (.X(main_1_out_3), .Y(main_1_out_3), .out_3(main_2_out_3));
  IICSE_012_Ass_1_a_main main_3 (.X(main_1_out_3), .Y(main_1_out_3), .out_3(main_3_out_3));
  IICSE_012_Ass_1_a_main main_4 (.X(main_2_out_3), .Y(main_3_out_3), .out_3(_4__X_prime____4X));

  // Notes on the sheet:
  //   -X
  //   -2X
  //   -2X
  //   -4X
  //   OUTPUT : 4x(X') = -4x
endmodule
