// Logisim project IICSE_012_Ass_8_5.circ as structural Verilog: 1 circuit, main circuit main
module main (
  input  [7:0] A,
  input  [7:0] X,
  output [7:0] A__X_6
);

  wire [7:0] main_1_out_3;

  IICSE_012_Ass_1_g_main main_1 (.X(X), .out_3(main_1_out_3));  // open: Y
  IICSE_012_Ass_1_e_main main_2 (.X(A), .Y(main_1_out_3), .out_3(A__X_6));

  // Notes on the sheet:
  //   X^6
  //   Imported from Ass 7
  //   Imported from Ass 7
  //   A.(X^6)
  //   OUTPUT: A x (X^6)
endmodule
