// Logisim project IICSE_012_Ass_9_2.circ as structural Verilog: 1 circuit, main circuit main
module main (
  input  a,
  input  b,
  input  F,
  output A_2,
  output B_2,
  output C,
  output D
);

  wire not_1_out, not_2_out;

  not not_1 (not_1_out, a);
  not not_2 (not_2_out, b);
  and and_1 (A_2, F, not_2_out, not_1_out);
  and and_2 (B_2, F, not_2_out, a);
  and and_3 (C, F, b, not_1_out);
  and and_4 (D, F, b, a);

  // Notes on the sheet:
  //   Assignment 9 
  //   4 Channel Demultiplexor Using Logic Gates
  //   U19CS012 
endmodule
