// Logisim project IICSE_012_Ass_9_1.circ as structural Verilog: 1 circuit, main circuit main
module main (
  input  D0,
  input  D1,
  input  D2,
  input  D3,
  input  D4,
  input  D5,
  input  D6,
  input  D7,
  input  S2,
  input  S1,
  input  S0,
  input  E_prime,
  output Y,
  output Y_prime
);

  wire and_1_out, and_2_out, and_3_out, and_4_out, and_5_out, and_6_out, and_7_out, and_8_out, not_1_out,
       not_2_out, not_3_out, not_4_out, not_5_out, not_6_out, not_7_out, not_8_out, or_1_out, undriven,
       undriven_2, undriven_3, undriven_4, undriven_5, undriven_6, undriven_7, undriven_8;

  not not_1 (not_1_out, S2);
  not not_2 (not_2_out, S1);
  not not_3 (not_3_out, S0);
  not not_4 (not_4_out, E_prime);
  not not_5 (not_5_out, not_1_out);
  not not_6 (not_6_out, not_2_out);
  not not_7 (not_7_out, not_3_out);
  and and_1 (and_1_out, undriven, not_1_out, not_2_out, not_3_out, not_4_out);
  and and_2 (and_2_out, undriven_2, not_1_out, not_2_out, not_7_out, not_4_out);
  and and_3 (and_3_out, undriven_3, not_1_out, not_6_out, not_3_out, not_4_out);
  and and_4 (and_4_out, undriven_4, not_1_out, not_2_out, not_7_out, not_4_out);
  or or_1 (or_1_out, and_1_out, and_2_out, and_3_out, and_4_out, and_5_out, and_6_out, and_7_out, and_8_out);
  not not_8 (not_8_out, or_1_out);
  and and_5 (and_5_out, undriven_5, not_5_out, not_2_out, not_3_out, not_4_out);
  and and_6 (and_6_out, undriven_6, not_2_out, not_5_out, not_7_out, not_4_out);
  and and_7 (and_7_out, undriven_7, not_6_out, not_5_out, not_3_out, not_4_out);
  and and_8 (and_8_out, undriven_8, not_7_out, not_6_out, not_4_out, not_5_out);

  // Notes on the sheet:
  //   Assignment 9
  //   8 : 1 Multiplexor
  //   U19CS012
endmodule
