// Logisim project U19CS012.circ as structural Verilog: 1 circuit, main circuit main
module main (
  input  [7:0] X,
  input  [7:0] Y,
  input  [7:0] Z,
  output [7:0] out_4
);

  wire adder_1_cout;
  wire [7:0] adder_1_out, adder_2_out;

  Adder adder_1 (.a(X), .b(Y), .out(adder_1_out), .cout(adder_1_cout));  // open: cin
  Adder adder_2 (.a(adder_1_out), .b(Z), .out(adder_2_out), .cin(adder_1_cout));  // open: cout
  Divider divider_1 (.a(adder_2_out), .b(8'h3), .out(out_4));  // open: upper, rem

  // Notes on the sheet:
  //   INPUT = X
  //   INPUT = Y
  //   INPUT = Z
  //   ADDER
  //   EVALUATION OF CO [BY MITALI MAM]
  //   U19CS012 [BHAGYA VINOD RANA]
  //   AIM : TO GENERATE (X+Y+Z)/3
  //   ADDER
  //   OUTPUT = (X + Y + Z)/3
  //   DIVIDER
endmodule
